// Logisim project Lab12.circ as structural Verilog: 10 circuits, main circuit Microprocessor
module Microprocessor (
  input  [15:0] Instruction,
  input  START,
  input  RESET,
  input  [3:0] Data_In,
  input  CLK,
  output [3:0] Address_Out,
  output [3:0] Data_Out,
  output Write_Enable,
  output READY
);

  wire Load_Signal_load, ROM_mode;
  wire [2:0] Datapath_pzn, ROM_condition, ROM_regb;
  wire [3:0] Operand_Select_constant;
  wire [7:0] CAR_ca, Data_Signal_cal, ROM_control_word_2;
  wire [15:0] ROM_control_word;

  Generate_Data_Signal_Logic Data_Signal (
    .NEXT_ADDRESS(ROM_control_word_2), .OPCODE(Instruction[15:12]), .START(START), .Mode(ROM_mode),
    .CAL(Data_Signal_cal));
  Generate_Load_Signal_Logic Load_Signal (
    .CA(CAR_ca), .PZN(Datapath_pzn), .Condition(ROM_condition), .Mode(ROM_mode), .START(START),
    .LOAD(Load_Signal_load));
  CAR CAR (.CAL(Data_Signal_cal), .LOAD(Load_Signal_load), .CLK(CLK), .CLR(RESET), .CA(CAR_ca));
  Control_Store__ROM ROM (
    .CA(CAR_ca), .RegB(ROM_regb), .Mode(ROM_mode), .Condition(ROM_condition),
    .Control_Word({ROM_control_word[15:12], ROM_control_word_2, ROM_control_word[3:0]}), .MW(Write_Enable));
  Operand_Select Operand_Select (
    .A(Instruction[11:8]), .B(Instruction[7:4]), .C(Instruction[3:0]), .RegB(ROM_regb),
    .Constant(Operand_Select_constant));
  Generate_Ready Ready_Signal (.CA(CAR_ca), .READY(READY));
  Lab11__Datapath Datapath (
    .CLK(CLK), .Control_Word({ROM_control_word[15:12], ROM_control_word_2, ROM_control_word[3:0]}),
    .constIn(Operand_Select_constant), .AddressOut(Address_Out), .DataOut(Data_Out), .PZN(Datapath_pzn),
    .DataIn(Data_In));
endmodule

module Generate_Data_Signal_Logic (
  input  [7:0] NEXT_ADDRESS,
  input  [3:0] OPCODE,
  input  START,
  input  Mode,
  output [7:0] CAL
);

  Multiplexer #(.select(2), .width(8), .enable("false")) multiplexer_1 (
    .in0({8{1'b0}}), .in1({OPCODE, 4'b0000}), .in2(NEXT_ADDRESS), .in3({OPCODE, 4'b0000}), .out(CAL),
    .sel({Mode, START}));
endmodule

module Generate_Load_Signal_Logic (
  input  [7:0] CA,
  input  [2:0] PZN,
  input  [2:0] Condition,
  input  Mode,
  input  START,
  output LOAD
);

  wire and_1_out, comparator_1_eq, multiplexer_1_out, or_1_out, or_2_out, or_3_out;

  Comparator comparator_1 (.a(CA), .b({8{1'b0}}), .eq(comparator_1_eq));  // open: gt, lt
  or or_1 (or_1_out, PZN[1], PZN[2]);
  or or_2 (or_2_out, PZN[2], PZN[0]);
  or or_3 (or_3_out, PZN[1], PZN[0]);
  Multiplexer #(.select(3), .enable("false")) multiplexer_1 (
    .in0(1'b0), .in1(PZN[2]), .in2(PZN[1]), .in3(or_1_out), .in4(PZN[0]), .in5(or_2_out), .in6(or_3_out),
    .in7(1'b1), .out(multiplexer_1_out), .sel(Condition));
  and and_1 (and_1_out, multiplexer_1_out, Mode);
  or or_4 (LOAD, comparator_1_eq, START, and_1_out);
endmodule

module CAR (
  input  [7:0] CAL,
  input  LOAD,
  input  CLK,
  input  CLR,
  output [7:0] CA
);

  wire d_ff_1_q, not_1_out;

  D_Flip_Flop d_ff_1 (.clk(CLK), .D(CLR), .Q(d_ff_1_q));  // open: Qn, preset, en, reset
  Counter CAR (.load(LOAD), .D(CAL), .count(not_1_out), .Q(CA), .clk(CLK), .clr(d_ff_1_q));  // open: carry
  not not_1 (not_1_out, LOAD);
endmodule

module Generate_Ready (
  input  [7:0] CA,
  output READY
);

  Comparator comparator_1 (.a(CA), .b({8{1'b0}}), .eq(READY));  // open: gt, lt
endmodule

module Control_Store__ROM (
  input  [7:0] CA,
  output [2:0] RegB,
  output Mode,
  output [2:0] Condition,
  output [15:0] Control_Word,
  output MW
);

  ROM #(.dataWidth(18)) rom_1 (
    .addr(CA), .data({Mode, MW, Control_Word[15], Condition, Control_Word[11:0]}));  // open: sel

  assign Control_Word[14:12] = Condition;
  assign RegB = Control_Word[11:9];

  // Notes on the sheet:
  //   ROM
  //   contents of rom_1 (hex, n*v repeats v):
  //   16*0 1031 11200 27000 13*0 1031 1233 2103 10200 27000 11*0 1031 1233 2103 1435 4105 2443 10200 27000
  //   8*0 1031 1233 2103 1435 4105 2453 10200 27000 8*0 1031 1233 2103 1435 4105 2463 10200 27000 8*0 1031
  //   1233 2103 20c3 10200 27000 10*0 1031 1233 2103 2083 10200 27000 10*0 1031 1233 2103 1435 4105 2493
  //   10200 27000 8*0 1031 1233 2103 1435 4105 4020 25000 10200 27000 7*0 1031 1233 2103 1435 4105 2450
  //   25aa0 3 10200 27000 13 10200 27000
  //   Microinstruction
endmodule

module Operand_Select (
  input  [3:0] A,
  input  [3:0] B,
  input  [3:0] C,
  input  [2:0] RegB,
  output [3:0] Constant
);

  Multiplexer #(.select(2), .width(4), .enable("false")) multiplexer_1 (
    .in0(A), .in1(B), .in2(C), .in3(C), .out(Constant), .sel(RegB[1:0]));
endmodule

module RAM (
  input  [3:0] Address,
  input  [3:0] DataIn,
  input  CLK,
  input  Load,
  output [3:0] DataOut
);

  wire not_1_out;

  assign DataOut = Load ? DataIn : 4'bz;  // Controlled_Buffer controlled_buffer_1
  RAM_part #(.addrWidth(4), .dataWidth(4)) ram_1 (
    .addr(Address), .data(DataOut), .clk(CLK), .ld(not_1_out));  // open: sel, clr
  not not_1 (not_1_out, Load);
endmodule

module Lab11__Datapath (
  input  CLK,
  input  [15:0] Control_Word,
  input  [3:0] constIn,
  input  [3:0] DataIn,
  output [3:0] AddressOut,
  output [3:0] DataOut,
  output [2:0] PZN
);

  wire and_1_out, and_2_out, and_4_out, and_5_out, and_6_out, and_7_out, and_8_out, and_9_out,
       comparator_2_eq, multiplexer_1_out, multiplexer_2_out, multiplexer_3_out, multiplexer_7_out,
       multiplexer_8_out, multiplexer_11_out, multiplexer_12_out, multiplexer_13_out;
  wire [3:0] adder_1_out, adder_2_out, and_3_out, divider_1_out, multiplexer_5_out, multiplexer_9_out,
       multiplexer_10_out, multiplier_1_out, not_1_out, or_1_out, R0_q, R1_q, R2_q, R3_q, R4_q, R5_q, R6_q,
       R7_q, shifter_1_out, shifter_2_out, shifter_3_out, subtractor_1_out;

  Multiplexer #(.select(3), .enable("false")) multiplexer_1 (
    .in0(1'b1), .in1(1'b0), .in2(1'b0), .in3(1'b0), .in4(1'b0), .in5(1'b0), .in6(1'b0), .in7(1'b0),
    .out(multiplexer_1_out), .sel(Control_Word[3:1]));
  and and_1 (and_1_out, Control_Word[0], multiplexer_1_out);
  Multiplexer #(.select(3), .enable("false")) multiplexer_2 (
    .in0(1'b0), .in1(1'b1), .in2(1'b0), .in3(1'b0), .in4(1'b0), .in5(1'b0), .in6(1'b0), .in7(1'b0),
    .out(multiplexer_2_out), .sel(Control_Word[3:1]));
  and and_2 (and_2_out, Control_Word[0], multiplexer_2_out);
  Register #(.width(4)) R0 (.D(multiplexer_10_out), .en(and_1_out), .Q(R0_q), .clk(CLK));  // open: clr
  Adder #(.width(4)) adder_1 (.a(AddressOut), .b(DataOut), .out(adder_1_out));  // open: cin, cout
  Subtractor #(.width(4)) subtractor_1 (.a(AddressOut), .b(DataOut), .out(subtractor_1_out));  // open: bin, bout
  Multiplier #(.width(4)) multiplier_1 (.a(AddressOut), .b(DataOut), .out(multiplier_1_out));  // open: cin, cout
  Divider #(.width(4)) divider_1 (.a(AddressOut), .b(DataOut), .out(divider_1_out));  // open: upper, rem
  assign not_1_out = ~AddressOut;  // NOT_Gate not_1, 4 bits wide
  assign and_3_out = AddressOut & DataOut;  // AND_Gate and_3, 4 bits wide
  assign or_1_out = AddressOut | DataOut;  // OR_Gate or_1, 4 bits wide
  Multiplexer #(.select(3), .enable("false")) multiplexer_3 (
    .in0(1'b0), .in1(1'b0), .in2(1'b1), .in3(1'b0), .in4(1'b0), .in5(1'b0), .in6(1'b0), .in7(1'b0),
    .out(multiplexer_3_out), .sel(Control_Word[3:1]));
  Register #(.width(4)) R1 (.D(multiplexer_10_out), .en(and_2_out), .Q(R1_q), .clk(CLK));  // open: clr
  Multiplexer #(.select(3), .width(4), .enable("false")) multiplexer_4 (
    .in0(R0_q), .in1(R1_q), .in2(R2_q), .in3(R3_q), .in4(R4_q), .in5(R5_q), .in6(R6_q), .in7(R7_q),
    .out(AddressOut), .sel(Control_Word[15:13]));
  Adder #(.width(4)) adder_2 (.a(not_1_out), .b(4'b0001), .out(adder_2_out));  // open: cin, cout
  Shifter #(.width(4), .shift("lr")) shifter_1 (.in(AddressOut), .\dist (2'b01), .out(shifter_1_out));
  Shifter #(.width(4)) shifter_2 (.in(AddressOut), .\dist (2'b01), .out(shifter_2_out));
  Shifter #(.width(4), .shift("ar")) shifter_3 (.in(AddressOut), .\dist (2'b01), .out(shifter_3_out));
  and and_4 (and_4_out, Control_Word[0], multiplexer_3_out);
  Register #(.width(4)) R2 (.D(multiplexer_10_out), .en(and_4_out), .Q(R2_q), .clk(CLK));  // open: clr
  Multiplexer #(.select(3), .width(4), .enable("false")) multiplexer_5 (
    .in0(R0_q), .in1(R1_q), .in2(R2_q), .in3(R3_q), .in4(R4_q), .in5(R5_q), .in6(R6_q), .in7(R7_q),
    .out(multiplexer_5_out), .sel(Control_Word[11:9]));
  Multiplexer #(.width(4), .enable("false")) multiplexer_6 (
    .in0(multiplexer_5_out), .in1(constIn), .out(DataOut), .sel(Control_Word[12]));
  Multiplexer #(.select(3), .enable("false")) multiplexer_7 (
    .in0(1'b0), .in1(1'b0), .in2(1'b0), .in3(1'b1), .in4(1'b0), .in5(1'b0), .in6(1'b0), .in7(1'b0),
    .out(multiplexer_7_out), .sel(Control_Word[3:1]));
  and and_5 (and_5_out, Control_Word[0], multiplexer_7_out);
  Register #(.width(4)) R3 (.D(multiplexer_10_out), .en(and_5_out), .Q(R3_q), .clk(CLK));  // open: clr
  Multiplexer #(.select(3), .enable("false")) multiplexer_8 (
    .in0(1'b0), .in1(1'b0), .in2(1'b0), .in3(1'b0), .in4(1'b1), .in5(1'b0), .in6(1'b0), .in7(1'b0),
    .out(multiplexer_8_out), .sel(Control_Word[3:1]));
  and and_6 (and_6_out, Control_Word[0], multiplexer_8_out);
  Register #(.width(4)) R4 (.D(multiplexer_10_out), .en(and_6_out), .Q(R4_q), .clk(CLK));  // open: clr
  Multiplexer #(.select(4), .width(4), .enable("false")) multiplexer_9 (
    .in0(4'b0000), .in1(4'b0001), .in2(AddressOut), .in3(DataOut), .in4(adder_1_out), .in5(subtractor_1_out),
    .in6(multiplier_1_out), .in7(divider_1_out), .in8(not_1_out), .in9(and_3_out), .in10(or_1_out),
    .in11(adder_2_out), .in12(shifter_1_out), .in13(shifter_2_out), .in14(shifter_3_out), .in15(4'b0000),
    .out(multiplexer_9_out), .sel(Control_Word[7:4]));
  Multiplexer #(.width(4), .enable("false")) multiplexer_10 (
    .in0(multiplexer_9_out), .in1(DataIn), .out(multiplexer_10_out), .sel(Control_Word[8]));
  Multiplexer #(.select(3), .enable("false")) multiplexer_11 (
    .in0(1'b0), .in1(1'b0), .in2(1'b0), .in3(1'b0), .in4(1'b0), .in5(1'b1), .in6(1'b0), .in7(1'b0),
    .out(multiplexer_11_out), .sel(Control_Word[3:1]));
  and and_7 (and_7_out, Control_Word[0], multiplexer_11_out);
  Register #(.width(4)) R5 (.D(multiplexer_10_out), .en(and_7_out), .Q(R5_q), .clk(CLK));  // open: clr
  Comparator #(.width(1)) comparator_1 (.a(1'b1), .b(multiplexer_9_out[3]), .eq(PZN[0]));  // open: gt, lt
  Comparator #(.width(4)) comparator_2 (.a(multiplexer_9_out), .b(4'b0000), .eq(comparator_2_eq));  // open: gt, lt
  not not_2 (PZN[1], comparator_2_eq);
  Multiplexer #(.select(3), .enable("false")) multiplexer_12 (
    .in0(1'b0), .in1(1'b0), .in2(1'b0), .in3(1'b0), .in4(1'b0), .in5(1'b0), .in6(1'b1), .in7(1'b0),
    .out(multiplexer_12_out), .sel(Control_Word[3:1]));
  and and_8 (and_8_out, Control_Word[0], multiplexer_12_out);
  Register #(.width(4)) R6 (.D(multiplexer_10_out), .en(and_8_out), .Q(R6_q), .clk(CLK));  // open: clr
  not not_3 (PZN[2], PZN[0]);
  Multiplexer #(.select(3), .enable("false")) multiplexer_13 (
    .in0(1'b0), .in1(1'b0), .in2(1'b0), .in3(1'b0), .in4(1'b0), .in5(1'b0), .in6(1'b0), .in7(1'b1),
    .out(multiplexer_13_out), .sel(Control_Word[3:1]));
  and and_9 (and_9_out, Control_Word[0], multiplexer_13_out);
  Register #(.width(4)) R7 (.D(multiplexer_10_out), .en(and_9_out), .Q(R7_q), .clk(CLK));  // open: clr

  // Notes on the sheet:
  //   D Address
  //   RegfileWrite
  //   A Address
  //   B Address
  //   MuxB
  //   Function Select
  //   MuxF
endmodule

module Main (
  input  [15:0] Instruction,
  input  START,
  input  RESET,
  output READY
);

  wire CLK_out, Microprocessor_write_enable;
  wire [3:0] Microprocessor_address_out, Microprocessor_data_out, RAM_dataout;

  Clock CLK (.out(CLK_out));
  Microprocessor Microprocessor (
    .Instruction(Instruction), .START(START), .RESET(RESET), .CLK(CLK_out),
    .Address_Out(Microprocessor_address_out), .Data_Out(Microprocessor_data_out),
    .Write_Enable(Microprocessor_write_enable), .Data_In(RAM_dataout), .READY(READY));
  RAM RAM (
    .Address(Microprocessor_address_out), .DataIn(Microprocessor_data_out), .CLK(CLK_out),
    .Load(Microprocessor_write_enable), .DataOut(RAM_dataout));
endmodule
